# Fritzing sketch cloudClock (saved by Fritzing 0.8.5b)
stripboards: 1
perfboards: 2

parts:
  Part1 = Arduino Yun
  LCD1 = LCD screen
  RE1 = Rotary Encoder [package=THT]
  R1 = Trimmer Potentiometer [maximum_resistance=10kΩ package=THT]
  S1 = Pushbutton [package="[THT]"]
  SP1 = SPEAKER [package=pcb_mount_speaker]  # not connected
  SP2 = SPEAKER [package=pcb_mount_speaker]  # not connected
  R2 = Resistor [tolerance=±5% resistance=220 package=THT]  # not connected
  R3 = Resistor [tolerance=±5% resistance=220 package=THT]  # not connected
  R4 = Resistor [tolerance=±5% resistance=220 package=THT]  # not connected
  R5 = Resistor [tolerance=±5% resistance=220 package=THT]  # not connected
  IC1 = Voltage Regulator [package=to220-igo]
  D1 = Diode [package=diode-1n4001]
  D2 = Diode [package=diode-1n4001]
  VCC1 = Battery block 9V

nets:
  N1: Part1.D8, LCD1.DB7
  N2: Part1.D9_PWM, LCD1.DB6
  N3: Part1.D10_PWM/SS, LCD1.DB5
  N4: Part1.D11_PWM/MOSI, LCD1.DB4
  N5: Part1.D12/MISO, LCD1.E
  N6: Part1.D13/SCK, LCD1.RS
  N7: Part1.D2, RE1.EncoderPinB
  N8: Part1.D3_PWM, RE1.EncoderPinA
  N9: Part1.D4, S1.Pin_3
  N10: Part1.D6_PWM, R1.leg1
  5V: Part1.5V, LCD1.VDD
  N11: Part1.GND, R1.leg2
  N12: LCD1.VSS, LCD1.R/W
  N13: LCD1.V0, R1.wiper
  N14: IC1.GND, D2.C
  N15: D1.A, VCC1.+

notes:
  Rotary encoder has a pushbutton by pushing the shaft
  32k/SQW/SCL/SDA/VCC/GND
  USB Soundcard

custom parts:
  Arduino Yun: The new Arduino Yun is a microcontroller board based on the ATmega32u4 (datasheet) and the Atheros AR9331. The Atheros processor supports a Linux distribution based on OpenWRT named Linino. The board has built-in Ethernet and WiFi support, a USB-A port, micro-SD card slot, 20 digital input/output pins (of which 7 can be used as PWM outputs and 12 as analog inputs), a 16 MHz crystal oscillator,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
